# Fritzing sketch relay_driver (saved by Fritzing 0.9.9b)
breadboards: 1

parts:
  U3 = RELAY [package=relay-t9a]
  D1 = Rectifier Diode [part_number=1N4007 package="Melf DO-213 AA [SMD]"]
  Q1 = TRANSISTOR_NPN [part_number=2N2222 package=to-92]
  LAMP = Incandescent light bulb small [package="bulb sm"]

nets:
  9V: U3.COIL1, D1.cathode
  N1: U3.COIL2, D1.anode, Q1.C
  N2: U3.MAIN, LAMP.1
  N3: U3.NC, LAMP.2
  GND: Q1.E
  V_iv: Q1.B

notes:
  AC Power
